# Fritzing sketch imdf-wiring (saved by Fritzing 0.9.3b)

parts:
  Raspberry_Pi_Zero1 = Raspberry Pi Zero
  Part1 = Adafruit Breadboard-Friendly NeoPixel [part_number="Adafruit #1312"]

nets:
  GND: Raspberry_Pi_Zero1.GND, Part1.GND
  N1: Raspberry_Pi_Zero1.GPIO18, Part1.IN
  5V: Raspberry_Pi_Zero1.5V, Part1.VDD

custom parts:
  Adafruit Breadboard-Friendly NeoPixel: This is the easiest way possible to add small, bright RGB pixels to your project. We took the same technology from our Flora NeoPixels and made them breadboard friendly, with two rows of 3 x 0.1" spaced header on each side for easy soldering, chaining and breadboarding. These ultra-bright LEDs have a constant-current driver cooked right into the LED package! The pixels are chainable - so you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
